// Logisim project fiz atoa.circ as structural Verilog: 1 circuit, main circuit QUESTAO 1 IACOM
module QUESTAO_1_IACOM (
  input  A,
  input  B,
  input  C,
  input  D,
  input  E,
  input  F,
  input  A_2,
  input  B_2,
  input  C_2,
  input  D_2,
  input  E_2,
  input  F_2,
  output out_13,
  output out_14
);

  wire and_1_out, and_2_out, and_3_out, and_4_out, and_5_out, and_6_out, and_7_out, and_8_out, and_9_out,
       and_10_out, not_1_out, not_2_out, not_3_out, not_4_out, not_5_out, not_6_out, not_7_out, not_8_out,
       not_9_out, or_1_out, or_3_out;

  not not_1 (not_1_out, B_2);
  not not_2 (not_2_out, A_2);
  not not_3 (not_3_out, C_2);
  not not_4 (not_4_out, E_2);
  not not_5 (not_5_out, A);
  not not_6 (not_6_out, B);
  not not_7 (not_7_out, C);
  not not_8 (not_8_out, E);
  not not_9 (not_9_out, F);
  and and_1 (and_1_out, not_2_out, not_1_out, not_3_out);
  and and_2 (and_2_out, not_3_out, F_2);
  and and_3 (and_3_out, not_3_out, E_2);
  and and_4 (and_4_out, C_2, D_2, not_4_out);
  or or_1 (or_1_out, not_5_out, not_6_out);
  and and_5 (and_5_out, A_2, not_1_out, D_2);
  and and_6 (and_6_out, A, not_6_out, D);
  and and_7 (and_7_out, C, not_8_out, D);
  or or_2 (out_14, and_5_out, and_1_out, and_2_out, and_3_out, and_4_out);
  or or_3 (or_3_out, and_6_out, and_7_out);
  and and_8 (and_8_out, or_1_out, not_7_out);
  and and_9 (and_9_out, not_7_out, F);
  and and_10 (and_10_out, not_7_out, E, not_9_out);
  or or_4 (out_13, and_8_out, or_3_out, and_9_out, and_10_out);

  // Notes on the sheet:
  //   CIRCUITO SIMPLIFICADO
  //   A'+B'
  //   AB'D+CE'D
  //   C'EF'
  //   (A'+B')C
  //   C'F
endmodule
